# Fritzing sketch CPX_AlligatorClips_RedCableToBlackCable (saved by Fritzing 0.9.5d)

parts:
  CLIP2 = Alligator Clip
  Part1 = Adafruit Circuit Playground Express [part_number="Adafruit #3333"]  # not connected
  CLIP3 = Alligator Clip
  CLIP6 = Alligator Clip
  CLIP7 = Alligator Clip

nets:
  N1: CLIP2.wire, CLIP6.wire
  N2: CLIP3.wire, CLIP7.wire

custom parts:
  Alligator Clip: Alligator clip
  Adafruit Circuit Playground Express: Circuit Playground Express is the next step towards a perfect introduction to electronics and programming. We've taken the original Circuit Playground Classic and made it even better! Not only did we pack even more sensors in, we also made it even easier to program. You can now start your journey with Microsoft MakeCode block-based or Javascript programming. Then, you can use the same board to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
  Alligator Clip: Alligator clip
