# Fritzing sketch CPX_SoftPot (saved by Fritzing 0.9.5d)

parts:
  CLIP5 = Alligator Clip
  Part2 = Adafruit Circuit Playground Express [part_number="Adafruit #3333"]  # not connected
  CLIP6 = Alligator Clip
  R2 = Resistor [tolerance=±5% resistance=10k package=THT]
  CLIP7 = Alligator Clip
  SparkFun1 = SoftPot Membrane Potentiometer - 50mm [part_number=SEN-08680]
  R1 = Resistor [tolerance=±5% resistance=10k package=THT]
  C2 = Ceramic Capacitor [capacitance=100nF package="200 mil [THT, multilayer]"]
  R3 = Resistor [tolerance=±5% resistance=100k package=THT]

nets:
  N1: CLIP5.wire, R1.Pin_0
  N2: CLIP6.wire, C2.1
  N3: R2.Pin_0, SparkFun1.leg2, R3.Pin_1
  N4: CLIP7.wire, SparkFun1.wiper, C2.0, R3.Pin_0
  N5: SparkFun1.leg1, R1.Pin_1

notes:
  0.47 uF

custom parts:
  Alligator Clip: Alligator clip
  Adafruit Circuit Playground Express: Circuit Playground Express is the next step towards a perfect introduction to electronics and programming. We've taken the original Circuit Playground Classic and made it even better! Not only did we pack even more sensors in, we also made it even easier to program. You can now start your journey with Microsoft MakeCode block-based or Javascript programming. Then, you can use the same board to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
  Alligator Clip: Alligator clip
  Alligator Clip: Alligator clip
  SoftPot Membrane Potentiometer - 50mm: These are very thin variable potentiometers. By pressing down on various parts of the strip, the resistance linearly changes from 100Ohms to 10,000Ohms allowing the user to very accurately calculate the relative position on the strip. Can be used as an accurate positional indicator for CNC head positioning, variable user input (volume level input for example), straight user input (multiple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
