# Fritzing sketch CPX_TwoPots (saved by Fritzing 0.9.5d)

parts:
  CLIP2 = Alligator Clip
  Part1 = Adafruit Circuit Playground Express [part_number="Adafruit #3333"]  # not connected
  CLIP3 = Alligator Clip
  CLIP4 = Alligator Clip
  R1 = Rotary Potentiometer (Small) [maximum_resistance=100kΩ package=THT]
  CLIP5 = Alligator Clip
  CLIP6 = Alligator Clip
  R2 = Rotary Potentiometer (Small) [maximum_resistance=100kΩ package=THT]  # not connected
  R3 = Rotary Potentiometer (Small) [maximum_resistance=100kΩ package=THT]  # not connected
  R4 = Rotary Potentiometer (Small) [maximum_resistance=100kΩ package=THT]
  CLIP7 = Alligator Clip

nets:
  N1: CLIP2.wire, R1.leg1
  N2: CLIP3.wire, R1.leg2
  N3: CLIP4.wire, R1.wiper
  N4: CLIP5.wire, R4.wiper
  N5: CLIP6.wire, R4.leg2
  N6: R4.leg1, CLIP7.wire

custom parts:
  Alligator Clip: Alligator clip
  Adafruit Circuit Playground Express: Circuit Playground Express is the next step towards a perfect introduction to electronics and programming. We've taken the original Circuit Playground Classic and made it even better! Not only did we pack even more sensors in, we also made it even easier to program. You can now start your journey with Microsoft MakeCode block-based or Javascript programming. Then, you can use the same board to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
  Alligator Clip: Alligator clip
  Alligator Clip: Alligator clip
  Alligator Clip: Alligator clip
