# Fritzing sketch ESP32-S3-pot-fade-no-breadboard (saved by Fritzing 0.9.5d)

parts:
  R1 = Resistor [tolerance=±5% resistance=220 package=THT]
  LED1 = LED - 5mm [color="Red (633nm)" package="5 mm [THT]"]
  Part1 = Adafruit ESP32-S3 Feather [part_number="Adafruit #5323"]
  POT1 = Breadboard Trimpot

nets:
  N1: R1.Pin_0, Part1.GND, POT1.PIN3
  N2: R1.Pin_1, LED1.cathode
  N3: LED1.anode, Part1.D13
  N4: Part1.A5, POT1.PIN2
  N5: Part1.3.3V, POT1.PIN1

custom parts:
  Adafruit ESP32-S3 Feather: The ESP32-S3 has arrived in Feather format - and what a great way to get started with this powerful new chip from Espressif! With dual 240 MHz cores, WiFi and BLE support, and native USB, this Feather is great for powering your IoT projects. That's right - it's the new Adafruit ESP32-S3 Feather! With native USB and 8 MB flash, this board will let you upgrade your existing ESP32 projects.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
