# Fritzing sketch ESP32-S3-pot-fade (saved by Fritzing 0.9.5d)
breadboards: 1

parts:
  Part1 = Adafruit ESP32-S3 Feather [part_number="Adafruit #5323"]
  R1 = Resistor [tolerance=±5% resistance=220 package=THT]
  LED1 = LED - 5mm [color="Red (633nm)" package="5 mm [THT]"]
  POT1 = Breadboard Trimpot

nets:
  N1: Part1.GND, Part1.A2, R1.Pin_1, POT1.PIN1
  N2: Part1.A5, POT1.PIN2
  N3: Part1.3.3V, POT1.PIN3
  N4: Part1.D13, LED1.anode
  N5: R1.Pin_0, LED1.cathode

custom parts:
  Adafruit ESP32-S3 Feather: The ESP32-S3 has arrived in Feather format - and what a great way to get started with this powerful new chip from Espressif! With dual 240 MHz cores, WiFi and BLE support, and native USB, this Feather is great for powering your IoT projects. That's right - it's the new Adafruit ESP32-S3 Feather! With native USB and 8 MB flash, this board will let you upgrade your existing ESP32 projects.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
