# Fritzing sketch ESP32-S3-tone-no-breadboard (saved by Fritzing 0.9.5d)

parts:
  Piezo_Buzzer = Piezo Speaker
  Part1 = Adafruit ESP32-S3 Feather [part_number="Adafruit #5323"]

nets:
  N1: Piezo_Buzzer.pin1, Part1.GND
  N2: Piezo_Buzzer.pin2, Part1.D13

custom parts:
  Adafruit ESP32-S3 Feather: The ESP32-S3 has arrived in Feather format - and what a great way to get started with this powerful new chip from Espressif! With dual 240 MHz cores, WiFi and BLE support, and native USB, this Feather is great for powering your IoT projects. That's right - it's the new Adafruit ESP32-S3 Feather! With native USB and 8 MB flash, this board will let you upgrade your existing ESP32 projects.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
