# Fritzing sketch ArduinoLeonardo_2Pots_WithBreadboard (saved by Fritzing 0.9.4)
breadboards: 1

parts:
  Part1 = Arduino Leonardo (Rev3b)
  Pot1 = POT [package=alps_pot]
  Pot2 = POT [package=alps_pot]

nets:
  N1: Part1.5V, Pot1.E, Pot2.E
  GND: Part1.GND, Pot1.A, Pot2.A
  N2: Part1.A0, Pot1.S
  N3: Part1.A1, Pot2.S
