# Fritzing sketch ArduinoUno_Blink3 (saved by Fritzing 0.9.3b)

parts:
  R6 = Resistor [tolerance=±5% resistance=220 package=THT]
  LED6 = LED - 5mm [color="Red (633nm)" package="5 mm [THT]"]
  R7 = Resistor [tolerance=±5% resistance=220 package=THT]
  LED7 = LED - 5mm [color="Red (633nm)" package="5 mm [THT]"]
  R8 = Resistor [tolerance=±5% resistance=220 package=THT]
  LED8 = LED - 5mm [color="Red (633nm)" package="5 mm [THT]"]

nets:
  N1: R6.Pin_0, LED6.cathode
  GND: R6.Pin_1, R7.Pin_1, R8.Pin_1
  Pin 2: LED6.anode
  N2: R7.Pin_0, LED7.cathode
  Pin 5: LED7.anode
  N3: R8.Pin_0, LED8.cathode
  Pin 9: LED8.anode
