# Fritzing sketch ArduinoUno_Blink_Pin3 (saved by Fritzing 0.9.3b)
breadboards: 2

parts:
  Part3 = Arduino Uno (Rev3)
  R5 = Resistor [tolerance=±5% resistance=220 package="1206 [SMD]"]
  LED1 = LED - 5mm [color="Red (633nm)" package="5 mm [THT]"]
  Part4 = Arduino Uno (Rev3)
  LED2 = LED - 5mm [color="Red (633nm)" package="5 mm [THT]"]
  R6 = Resistor [tolerance=±5% resistance=220 package="1206 [SMD]"]

nets:
  N1: Part3.GND, LED1.cathode
  N2: Part3.D3_PWM, R5.Pin_0
  N3: R5.Pin_1, LED1.anode
  N4: Part4.GND, LED2.cathode
  N5: LED2.anode, R6.Pin_0
