# Fritzing sketch ArduinoUno_ButtonPlusLED (saved by Fritzing 0.9.4)
breadboards: 1

parts:
  Part7 = Arduino Uno (Rev3)
  R1 = Resistor [tolerance=±5% resistance=10k package="1206 [SMD]"]
  S7 = Momentary Switch [package=ksa_sealed_tac_switch]
  R2 = Resistor [tolerance=±5% resistance=220 package=THT]
  LED1 = LED - 5mm [color="Red (633nm)" package="5 mm [THT]"]

nets:
  N1: Part7.D2, R1.Pin_1, S7.4
  N2: Part7.D3_PWM, R2.Pin_0
  N3: Part7.5V, S7.2
  GND: Part7.GND, R1.Pin_0, LED1.cathode
  N4: R2.Pin_1, LED1.anode
