# Fritzing sketch ArduinoUno_Button_CircuitSchematic (saved by Fritzing 0.9.4)

parts:
  S6 = Momentary Switch [package=ksa_sealed_tac_switch]
  R8 = Resistor [tolerance=±5% resistance=10k package="1206 [SMD]"]
  V1 = DC Power [voltage=5]
  S7 = Momentary Switch [package=ksa_sealed_tac_switch]
  V2 = DC Power [voltage=5]
  R10 = Resistor [tolerance=±5% resistance=10k package="1206 [SMD]"]
  S9 = Round Pushbutton
  R11 = Resistor [tolerance=±5% resistance=10k package="1206 [SMD]"]
  V3 = DC Power [voltage=5]
  R12 = Resistor [tolerance=±5% resistance=10k package="1206 [SMD]"]
  V4 = DC Power [voltage=5]
  S10 = Round Pushbutton
  S11 = Momentary Switch [package=ksa_sealed_tac_switch]
  R13 = Resistor [tolerance=±5% resistance=10k package="1206 [SMD]"]
  V6 = DC Power [voltage=5]
  S12 = Momentary Switch [package=ksa_sealed_tac_switch]
  R14 = Resistor [tolerance=±5% resistance=10k package="1206 [SMD]"]
  V8 = DC Power [voltage=5]
  S13 = Momentary Switch [package=ksa_sealed_tac_switch]
  R15 = Resistor [tolerance=±5% resistance=10k package="1206 [SMD]"]
  S14 = Round Pushbutton

nets:
  N1: S6.2, V1.V+
  Pin 2: S6.4, R8.Pin_0, S7.2, R10.Pin_1, S11.2, R13.Pin_1, S12.4, R14.Pin_0, S13.4, R15.Pin_0
  GND: R8.Pin_1, S7.4, R11.Pin_0, S10.leg0, R13.Pin_0, S12.2, S13.2
  N2: V2.V+, R10.Pin_0
  Digital Input Pin .: S9.leg0, R11.Pin_1, R12.Pin_0, S10.leg1
  N3: S9.leg1, V3.V-
  N4: R12.Pin_1, V4.V-
  N5: S11.4, V6.V+
  N6: R14.Pin_1, V8.V+
  N7: R15.Pin_1, S14.leg1
  5V: S14.leg0

notes:
  Pull-down
  Pull-up
  Internal pull-up resistor
