# Fritzing sketch ArduinoUno_Button_CircuitSchematic_v2 (saved by Fritzing 0.9.4)

parts:
  S6 = Momentary Switch [package=ksa_sealed_tac_switch]
  R8 = Resistor [tolerance=±5% resistance=10k package="1206 [SMD]"]
  S7 = Momentary Switch [package=ksa_sealed_tac_switch]
  R10 = Resistor [tolerance=±5% resistance=10k package="1206 [SMD]"]
  S9 = Round Pushbutton
  R11 = Resistor [tolerance=±5% resistance=10k package="1206 [SMD]"]
  R12 = Resistor [tolerance=±5% resistance=10k package="1206 [SMD]"]
  S10 = Round Pushbutton
  S11 = Momentary Switch [package=ksa_sealed_tac_switch]
  R13 = Resistor [tolerance=±5% resistance=10k package="1206 [SMD]"]
  S12 = Momentary Switch [package=ksa_sealed_tac_switch]
  R14 = Resistor [tolerance=±5% resistance=10k package="1206 [SMD]"]
  S13 = Momentary Switch [package=ksa_sealed_tac_switch]
  R15 = Resistor [tolerance=±5% resistance=10k package="1206 [SMD]"]
  S14 = Round Pushbutton
  S17 = Pushbutton [package="[SMD]"]  # not connected
  S19 = Round Pushbutton
  S20 = Round Pushbutton
  S21 = Round Pushbutton
  R16 = Resistor [tolerance=±5% resistance=10k package="1206 [SMD]"]

nets:
  5V: S6.2, R10.Pin_0, S9.leg1, R12.Pin_1, S11.4, R14.Pin_1, S14.leg0, S19.leg1, S20.leg1, S21.leg1
  Pin 2: S6.4, R8.Pin_0, S7.2, R10.Pin_1, S11.2, R13.Pin_1, S12.4, R14.Pin_0, S13.4, R15.Pin_0
  Digital Input Pin/GND: R8.Pin_1, S7.4, S9.leg0, R11.Pin_0, R11.Pin_1, R12.Pin_0, S10.leg0, S10.leg1, R13.Pin_0, S12.2, S13.2, S19.leg0, S20.leg0, S21.leg0, R16.Pin_0, R16.Pin_1
  N1: R15.Pin_1, S14.leg1

notes:
  Pull-down
  Pull-up
  Internal pull-up resistor
  Walkthrough
