# Fritzing sketch ArduinoUno_Button_Pin2 (saved by Fritzing 0.9.4)
breadboards: 9

parts:
  Part3 = Arduino Uno (Rev3)
  R5 = Resistor [tolerance=±5% resistance=10k package="1206 [SMD]"]
  S3 = Momentary Switch [package=ksa_sealed_tac_switch]
  Part4 = Arduino Uno (Rev3)
  S4 = Momentary Switch [package=ksa_sealed_tac_switch]
  R7 = Resistor [tolerance=±5% resistance=10k package="1206 [SMD]"]
  Part5 = Arduino Uno (Rev3)
  S5 = Momentary Switch [package=ksa_sealed_tac_switch]
  R8 = Resistor [tolerance=±5% resistance=10k package="1206 [SMD]"]
  Part6 = Arduino Uno (Rev3)
  R9 = Resistor [tolerance=±5% resistance=10k package="1206 [SMD]"]
  S6 = Momentary Switch [package=ksa_sealed_tac_switch]
  Part7 = Arduino Uno (Rev3)
  S7 = Momentary Switch [package=ksa_sealed_tac_switch]
  R10 = Resistor [tolerance=±5% resistance=10k package="1206 [SMD]"]
  Part9 = Arduino Uno (Rev3)
  R11 = Resistor [tolerance=±5% resistance=10k package="1206 [SMD]"]
  S8 = Momentary Switch [package=ksa_sealed_tac_switch]
  Part10 = Arduino Uno (Rev3)
  S9 = Momentary Switch [package=ksa_sealed_tac_switch]
  Part11 = Arduino Uno (Rev3)
  S10 = Momentary Switch [package=ksa_sealed_tac_switch]
  Part12 = Arduino Uno (Rev3)
  S11 = Momentary Switch [package=ksa_sealed_tac_switch]

nets:
  N1: Part3.GND, R5.Pin_0
  N2: Part3.D2, R5.Pin_1, S3.4
  N3: Part3.5V, S3.2
  N4: Part4.GND, R7.Pin_1
  N5: Part4.D2, S4.4
  N6: Part4.5V, S4.1
  N7: S4.3, R7.Pin_0
  N8: Part5.GND, R8.Pin_1
  N9: Part5.D2, S5.4
  N10: Part5.5V, S5.2
  N11: S5.3, R8.Pin_0
  N12: Part6.D2, R9.Pin_1, S6.4
  N13: Part6.5V, S6.2
  N14: Part6.GND, R9.Pin_0
  N15: Part7.D2, S7.4
  N16: Part7.5V, S7.1
  N17: Part7.GND, R10.Pin_1
  N18: S7.3, R10.Pin_0
  N19: Part9.D2, R11.Pin_1, S8.2
  N20: Part9.5V, R11.Pin_0
  N21: Part9.GND, S8.4
  N22: Part10.D2, S9.2
  N23: Part10.GND, S9.4
  N24: Part11.D2, S10.4
  N25: Part11.5V, S10.2
  N26: Part12.D2, Part12.GND, S11.4
  N27: Part12.5V, S11.2

notes:
  Pull-down resistor configurations
  Pull-up resistor configuration
  Internal pull-up resistor configuration
  Incorrect walkthrough
