# Fritzing sketch ArduinoUno_FSRLEDCircuit (saved by Fritzing 0.9.4)
breadboards: 1

parts:
  Part8 = Arduino Uno (Rev3)
  R1 = Resistor [tolerance=±5% resistance=220 package=THT]
  LED = LED - 5mm [color="Red (633nm)" package="5 mm [THT]"]
  Slide_Pot = SLIDER [package=slider]

nets:
  N1: Part8.A0, Slide_Pot.S
  GND: Part8.GND, LED.cathode, Slide_Pot.A
  N2: Part8.D3_PWM, R1.Pin_0
  N3: Part8.5V, Slide_Pot.E
  N4: R1.Pin_1, LED.anode
