# Fritzing sketch ArduinoUno_FSR_PiezoBreadboard (saved by Fritzing 0.9.4)
breadboards: 1

parts:
  Part9 = Arduino Uno (Rev3)
  J3 = Basic Force Sensing Resistor (FSR) [package=THT]
  R1 = Resistor [tolerance=±5% resistance=10k package=THT]
  J4 = Piezo Speaker

nets:
  N1: Part9.A0, J3.pin_1, R1.Pin_0
  N2: Part9.D2, J4.pin2
  N3: Part9.5V, J3.pin_0
  N4: Part9.GND, R1.Pin_1, J4.pin1
