# Fritzing sketch ArduinoUno_FSR_VoltageDivider_Breadboard2 (saved by Fritzing 0.9.4)
breadboards: 4

parts:
  Part9 = Arduino Uno (Rev3)
  J3 = Basic Force Sensing Resistor (FSR) [package=THT]
  R1 = Resistor [tolerance=±5% resistance=10k package=THT]
  Part10 = Arduino Uno (Rev3)
  J4 = Basic Force Sensing Resistor (FSR) [package=THT]
  Part11 = Arduino Uno (Rev3)
  J5 = Basic Force Sensing Resistor (FSR) [package=THT]
  Part12 = Arduino Uno (Rev3)
  J6 = Basic Force Sensing Resistor (FSR) [package=THT]
  R2 = Resistor [tolerance=±5% resistance=10k package=THT]

nets:
  N1: Part9.A0, J3.pin_1, R1.Pin_0
  N2: Part9.5V, J3.pin_0
  N3: Part9.GND, R1.Pin_1
  N4: Part10.A0, J4.pin_1
  N5: Part10.5V, J4.pin_0
  N6: Part11.A0, J5.pin_0
  N7: Part11.5V, J5.pin_1
  N8: Part12.A0, J6.pin_0, R2.Pin_1
  N9: Part12.5V, R2.Pin_0
  N10: Part12.GND, J6.pin_1

notes:
  Incorrect
