# Fritzing sketch ArduinoUno_Photocell_Breadboard (saved by Fritzing 0.9.4)
breadboards: 4

parts:
  Part9 = Arduino Uno (Rev3)
  R1 = Resistor [tolerance=±5% resistance=10k package=THT]
  R2 = PHOTOCELL [package=photocell]
  R3 = Resistor [tolerance=±20% resistance=220 package=THT]
  LED1 = LED - 5mm [color="Red (633nm)" package="5 mm [THT]"]
  Part10 = Arduino Uno (Rev3)
  R4 = PHOTOCELL [package=photocell]
  R5 = Resistor [tolerance=±5% resistance=10k package=THT]
  Part11 = Arduino Uno (Rev3)
  Part12 = Arduino Uno (Rev3)
  R7 = PHOTOCELL [package=photocell]
  R9 = Resistor [tolerance=±5% resistance=10k package=THT]
  R10 = Resistor [tolerance=±20% resistance=220 package=THT]
  LED2 = LED - 5mm [color="Red (633nm)" package="5 mm [THT]"]
  R8 = Resistor [tolerance=±5% resistance=10k package=THT]
  R6 = PHOTOCELL [package=photocell]

nets:
  N1: Part9.A0, R1.Pin_0, R2.P$2
  N2: Part9.D3_PWM, R3.Pin_0
  N3: Part9.5V, R2.P$1
  N4: Part9.GND, R1.Pin_1, LED1.cathode
  N5: R3.Pin_1, LED1.anode
  N6: Part10.A0, R4.P$2, R5.Pin_0
  N7: Part10.5V, R4.P$1
  N8: Part10.GND, R5.Pin_1
  N9: Part11.A0, R8.Pin_1, R6.P$1
  N10: Part11.D3_PWM, R10.Pin_0
  N11: Part11.5V, R8.Pin_0
  N12: Part11.GND, LED2.cathode, R6.P$2
  N13: Part12.A0, R7.P$1, R9.Pin_1
  N14: Part12.5V, R9.Pin_0
  N15: Part12.GND, R7.P$2
  N16: R10.Pin_1, LED2.anode

notes:
  "Lightness" configuration
  "Darkness" configuration
