# Fritzing sketch ArduinoUno_Photocell_PiezoBreadboard (saved by Fritzing 0.9.4)
breadboards: 1

parts:
  Part9 = Arduino Uno (Rev3)
  R1 = Resistor [tolerance=±5% resistance=10k package=THT]
  J4 = Piezo Speaker
  R2 = PHOTOCELL [package=photocell]

nets:
  N1: Part9.A0, R1.Pin_0, R2.P$2
  N2: Part9.D2, J4.pin2
  N3: Part9.5V, R2.P$1
  N4: Part9.GND, R1.Pin_1, J4.pin1
