# Fritzing sketch ArduinoUno_Potentiometer (saved by Fritzing 0.9.4)
breadboards: 1

parts:
  Part8 = Arduino Uno (Rev3)
  Pot = TRIMPOT [package=3362u-2]

nets:
  N1: Part8.A0, Pot.WIPER
  GND: Part8.GND, Pot.CCW
  N2: Part8.5V, Pot.CW
