# Fritzing sketch ArduinoUno_PotentiometerLEDCircuit (saved by Fritzing 0.9.4)
breadboards: 1

parts:
  Part8 = Arduino Uno (Rev3)
  R1 = Resistor [tolerance=±5% resistance=220 package=THT]
  LED = LED - 5mm [color="Red (633nm)" package="5 mm [THT]"]
  J5 = Basic Force Sensing Resistor (FSR) [package=THT]
  R2 = Resistor [tolerance=±5% resistance=10k package=THT]

nets:
  N1: Part8.A0, J5.pin_1, R2.Pin_0
  GND: Part8.GND, LED.cathode, J5.pin_0
  N2: Part8.D3_PWM, R1.Pin_0
  N3: Part8.5V, R2.Pin_1
  N4: R1.Pin_1, LED.anode
