# Fritzing sketch ArduinoUno_Potentiometer_CorrectAndIncorrect_Schematic2 (saved by Fritzing 0.9.4)

parts:
  J4 = Basic Force Sensing Resistor (FSR) [package=THT]
  R2 = Resistor [tolerance=±5% resistance=10k package=THT]
  R3 = Trimmer Potentiometer [maximum_resistance=10kΩ package=THT]

nets:
  5V: J4.pin_0, R3.leg2
  Input Pin A0: J4.pin_1, R2.Pin_0
  GND: R2.Pin_1
