# Fritzing sketch BasicLEDCircuitSchematic (saved by Fritzing 0.9.4)

parts:
  R1 = Resistor [tolerance=±5% resistance=220 package=THT]
  LED1 = LED - 5mm [color="Red (633nm)" package="5 mm [THT]"]
  V1 = DC Power [voltage=5]
  R2 = Resistor [tolerance=±5% resistance=220 package=THT]
  LED2 = LED - 5mm [color="Red (633nm)" package="5 mm [THT]"]
  R3 = Resistor [tolerance=±5% resistance=220 package=THT]
  LED3 = LED - 5mm [color="Red (633nm)" package="5 mm [THT]"]
  V2 = DC Power [voltage=5]
  R4 = Resistor [tolerance=±5% resistance=220 package=THT]
  R5 = Resistor [tolerance=±5% resistance=220 package=THT]
  R6 = Resistor [tolerance=±5% resistance=220 package=THT]
  LED4 = LED - 5mm [color="Red (633nm)" package="5 mm [THT]"]
  LED5 = LED - 5mm [color="Red (633nm)" package="5 mm [THT]"]
  LED6 = LED - 5mm [color="Red (633nm)" package="5 mm [THT]"]

nets:
  N1: R1.Pin_0, LED1.anode
  N2: R1.Pin_1, V1.V-
  GND: LED1.cathode, R2.Pin_1, R5.Pin_1
  N3: R2.Pin_0, LED2.cathode
  Pin 3: LED2.anode, LED5.anode
  N4: R3.Pin_0, LED3.anode
  N5: R3.Pin_1, V2.V-
  Pin 4: LED3.cathode, LED4.cathode
  N6: R4.Pin_0, LED4.anode
  5V: R4.Pin_1, R6.Pin_1
  N7: R5.Pin_0, LED5.cathode
  N8: R6.Pin_0, LED6.anode
