# Fritzing sketch BasicResistorBatteryCircuit_Diagram (saved by Fritzing 0.9.4)

parts:
  R1 = Resistor [tolerance=±5% resistance=100 package=THT]
  U1 = BATTERY-2 [package=battery-aa]
  R2 = Resistor [tolerance=±5% resistance=100 package=THT]
  U2 = BATTERY-2 [package=battery-aa]
  U3 = BATTERY-2 [package=battery-aa]
  R3 = Resistor [tolerance=±5% resistance=50 package=THT]
  U4 = BATTERY-2 [package=battery-aa]
  R4 = Resistor [tolerance=±5% resistance=100 package=THT]
  R6 = Resistor [tolerance=±5% resistance=100 package=THT]
  U5 = BATTERY-2 [package=battery-aa]
  U7 = BATTERY-2 [package=battery-aa]
  U6 = BATTERY-2 [package=battery-aa]
  R7 = Resistor [tolerance=±5% resistance=50 package=THT]
  U8 = BATTERY-2 [package=battery-aa]
  VCC1 = Battery block 9V
  U9 = SWITCH_SPDT [package=kps-1290]

nets:
  N1: R1.Pin_0, U1.-1
  N2: R1.Pin_1, U1.+1
  N3: R2.Pin_0, U3.-1
  N4: R2.Pin_1, U2.+1
  N5: U2.-1, U3.+1
  N6: R3.Pin_0, U4.-1
  N7: R3.Pin_1, U4.+1
  N8: R4.Pin_0, U7.+1
  N9: R4.Pin_1, U7.-1
  N10: R6.Pin_0, U5.+1
  N11: R6.Pin_1, U6.-1
  N12: U5.-1, U6.+1
  N13: R7.Pin_0, U8.+1
  N14: R7.Pin_1, U8.-1
  N15: VCC1.+, U9.O
