# Fritzing sketch BasicResistorPlusIncadescentBatteryCircuit_Diagram (saved by Fritzing 0.9.4)

parts:
  R1 = Resistor [tolerance=±5% resistance=220 package=THT]
  U1 = BATTERY-2 [package=battery-aa]
  BULB1 = Incandescent light bulb small [package="bulb sm"]

nets:
  N1: R1.Pin_0, BULB1.1
  N2: R1.Pin_1, U1.+1
  N3: U1.-1, BULB1.2
