# Fritzing sketch BasicResistorPlusLEDBatteryCircuit_Diagram (saved by Fritzing 0.9.4)

parts:
  R1 = Resistor [tolerance=±5% resistance=220 package=THT]
  U1 = BATTERY-2 [package=battery-aa]
  LED2 = LED - 5mm [color="Red (633nm)" package="5 mm [THT]"]

nets:
  N1: R1.Pin_0, LED2.anode
  N2: R1.Pin_1, U1.+1
  N3: U1.-1, LED2.cathode
