# Fritzing sketch BreadboardExample2 (saved by Fritzing 0.9.4)
breadboards: 1

parts:
  VCC2 = Battery block 9V
  R1 = Resistor [tolerance=±5% resistance=220 package=THT]
  LED1 = LED - 5mm [color="Red (633nm)" package="5 mm [THT]"]

nets:
  N1: VCC2.-, LED1.cathode
  N2: VCC2.+, R1.Pin_0
  N3: R1.Pin_1, LED1.anode
