# Fritzing sketch BreadboardExample3 (saved by Fritzing 0.9.4)
breadboards: 1

parts:
  VCC2 = Battery block 9V
  R1 = Resistor [tolerance=±5% resistance=220 package=THT]  # not connected
  LED1 = LED - 5mm [color="Red (633nm)" package="5 mm [THT]"]

nets:
  N1: VCC2.-, LED1.cathode
