# Fritzing sketch BreadboardExample6 (saved by Fritzing 0.9.4)
breadboards: 1

parts:
  VCC2 = Battery block 9V
  LED1 = smd LED [color="Red (633nm)" package="0603 [SMD]"]
  R2 = Resistor [tolerance=±5% resistance=220 package=THT]

nets:
  N1: VCC2.-, LED1.cathode
  N2: VCC2.+, R2.Pin_1
  N3: LED1.anode, R2.Pin_0
