# Fritzing sketch Button_LEDCircuit_Breadboard2 (saved by Fritzing 0.9.4)
breadboards: 2

parts:
  Part7 = Arduino Uno (Rev3)
  S7 = Momentary Switch [package=ksa_sealed_tac_switch]
  R1 = Resistor [tolerance=±5% resistance=220 package=THT]
  LED1 = LED - 5mm [color="Red (633nm)" package="5 mm [THT]"]
  VCC1 = Battery block 9V
  S8 = Momentary Switch [package=ksa_sealed_tac_switch]
  R2 = Resistor [tolerance=±5% resistance=470 package=THT]
  LED2 = LED - 5mm [color="Red (633nm)" package="5 mm [THT]"]

nets:
  N1: Part7.5V, S7.2
  N2: Part7.GND, LED1.cathode
  N3: S7.4, R1.Pin_1
  N4: R1.Pin_0, LED1.anode
  N5: VCC1.-, LED2.cathode
  N6: VCC1.+, S8.3
  N7: S8.1, R2.Pin_0
  N8: R2.Pin_1, LED2.anode
