# Fritzing sketch Button_LEDCircuit_Schematic (saved by Fritzing 0.9.4)

parts:
  V1 = DC Power [voltage=5]
  S15 = Round Pushbutton
  R1 = Resistor [tolerance=±5% resistance=220 package=THT]
  LED1 = LED - 5mm [color="Red (633nm)" package="5 mm [THT]"]
  S16 = Pushbutton [package="[SMD]"]  # not connected
  S17 = Momentary Switch [package=ksa_sealed_tac_switch]  # not connected
  V2 = DC Power [voltage=5]
  R2 = Resistor [tolerance=±5% resistance=220 package=THT]
  LED2 = LED - 5mm [color="Red (633nm)" package="5 mm [THT]"]
  S18 = Momentary Switch [package=ksa_sealed_tac_switch]
  R3 = Resistor [tolerance=±5% resistance=220 package=THT]
  LED3 = LED - 5mm [color="Red (633nm)" package="5 mm [THT]"]
  S19 = Momentary Switch [package=ksa_sealed_tac_switch]
  S20 = Pushbutton [package="[SMD]"]  # not connected

nets:
  N1: V1.V+, S15.leg0
  N2: V1.V-, LED1.cathode
  N3: S15.leg1, R1.Pin_0
  N4: R1.Pin_1, LED1.anode
  N5: V2.V+, S18.1
  N6: V2.V-, LED2.cathode
  N7: R2.Pin_0, S18.3
  N8: R2.Pin_1, LED2.anode
  N9: R3.Pin_0, S19.3
  N10: R3.Pin_1, LED3.anode
  GND: LED3.cathode
  5V: S19.1
