# Fritzing sketch DiodeWith100OhmResistor (saved by Fritzing 0.9.4)

parts:
  VCC1 = Battery block 9V
  R1 = Resistor [tolerance=±5% resistance=100 package=THT]
  D1 = Rectifier Diode [part_number=1N4001 package="300 mil [THT]"]

nets:
  N1: VCC1.-, D1.cathode
  N2: VCC1.+, R1.Pin_1
  N3: R1.Pin_0, D1.anode
