# Fritzing sketch ExampleFritizingDiagramForLesson2Exercise-Backup (saved by Fritzing 0.9.4)

parts:
  VCC3 = Battery block 9V
  S9 = Pushbutton [package=THT]
  LED1 = smd LED [color="Red (633nm)" package="0603 [SMD]"]
  R3 = Resistor [tolerance=±5% resistance=470 package=THT]

nets:
  N1: VCC3.-, LED1.cathode
  N2: VCC3.+, S9.leg1
  N3: S9.leg0, R3.Pin_1
  N4: LED1.anode, R3.Pin_0
