# Fritzing sketch ExampleFritizingDiagramForLesson2Exercise-VersionMadeInYouTubeRecording (saved by Fritzing 0.9.4)

parts:
  VCC1 = Battery block 9V
  S1 = Pushbutton [package=THT]
  R1 = Resistor [tolerance=±5% resistance=470 package=THT]
  LED1 = LED - 5mm [color="Red (633nm)" package="5 mm [THT]"]

nets:
  N1: VCC1.-, LED1.cathode
  N2: VCC1.+, S1.leg1
  N3: S1.leg0, R1.Pin_1
  N4: R1.Pin_0, LED1.anode
