# Fritzing sketch FSRWithBreadboard (saved by Fritzing 0.9.4)
breadboards: 1

parts:
  VCC3 = Battery block 9V
  R1 = Resistor [tolerance=±5% resistance=330 package=THT]
  LED1 = LED - 5mm [color="Red (633nm)" package="5 mm [THT]"]
  J1 = Basic Force Sensing Resistor (FSR) [package=THT]

nets:
  N1: VCC3.-, LED1.cathode
  N2: VCC3.+, J1.pin_0
  N3: R1.Pin_0, J1.pin_1
  N4: R1.Pin_1, LED1.anode
