# Fritzing sketch FSR_LEDCircuit_Breadboard (saved by Fritzing 0.9.4)
breadboards: 2

parts:
  Part8 = Arduino Uno (Rev3)
  LED3 = LED - 5mm [color="Red (633nm)" package="5 mm [THT]"]
  LED4 = LED - 5mm [color="Red (633nm)" package="5 mm [THT]"]
  VCC2 = Battery block 9V
  J1 = Basic Force Sensing Resistor (FSR) [package=THT]
  J2 = Basic Force Sensing Resistor (FSR) [package=THT]
  R1 = Resistor [tolerance=±5% resistance=470 package=THT]

nets:
  N1: Part8.5V, J2.pin_1
  N2: Part8.GND, LED4.cathode
  N3: LED3.cathode, VCC2.-
  N4: LED3.anode, J1.pin_1
  N5: LED4.anode, J2.pin_0
  N6: VCC2.+, R1.Pin_0
  N7: J1.pin_0, R1.Pin_1
