# Fritzing sketch Feather_NeopixelStrand_StrandTestPot (saved by Fritzing 0.9.5d)
breadboards: 1

parts:
  Part1 = Adafruit Feather M0 Express [part_number="Adafruit #3403"]
  POT1 = Breadboard Trimpot
  POT2 = Breadboard Trimpot
  POT3 = Breadboard Trimpot
  NEOPIXEL1 = Neopixel Strip -- White (30/m) [part_number=1376]
  R1 = Resistor [tolerance=±5% resistance=470 package=THT]
  C1 = Electrolytic Capacitor [capacitance=1mF package="100 mil [THT, electrolytic]"]

nets:
  GND: Part1.GND, POT1.PIN1, POT1.PIN3, POT2.PIN1, POT2.PIN3, POT3.PIN1, POT3.PIN3, NEOPIXEL1.GND, C1.-
  N1: Part1.A3, POT3.PIN2
  N2: Part1.A2, POT2.PIN2
  N3: Part1.A1, POT1.PIN2
  +3V3: Part1.+3V3, NEOPIXEL1.+5V, C1.+
  N4: Part1.D5, R1.Pin_0
  N5: NEOPIXEL1.Din, R1.Pin_1

notes:
  NUM_NEOPIXELS_POT_PIN
  Controls num of NeoPixels to illuminate
  HUE_POT_PIN
  Controls hue of NeoPixels
  BRIGHTNESS_POT_PIN
  Controls brightness of NeoPixels

custom parts:
  Adafruit Feather M0 Express: We love all our Feathers equally, but this Feather is very special. It's our first Feather that is specifically designed for use with CircuitPython! CircuitPython is our beginner-oriented flavor of MicroPython - and as the name hints at, its a small but full-featured version of the popular Python programming language specifically for use with circuitry and electronics. That doesn't mean you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
  Neopixel Strip -- White (30/m): These NeoPixel strips have 30 digitally-addressable pixel LEDs per meter and are very affordable and are only 12.5 mm wide, 10 mm if you remove the strip from the casing.
