# Fritzing sketch Huzzah32_Blink_Diagram (saved by Fritzing 0.9.4)
breadboards: 1

parts:
  Part1 = Adafruit HUZZAH32 ESP32 Feather [part_number="Adafruit #3405"]
  R1 = Resistor [tolerance=±5% resistance=220 package=THT]
  LED1 = LED - 5mm [color="Red (633nm)" package="5 mm [THT]"]

nets:
  N1: Part1.IO21, R1.Pin_0
  N2: Part1.GND, LED1.cathode
  N3: R1.Pin_1, LED1.anode
