# Fritzing sketch Huzzah32_Photocell_DiagramAndSchematic (saved by Fritzing 0.9.4)
breadboards: 1

parts:
  Part1 = Adafruit HUZZAH32 ESP32 Feather [part_number="Adafruit #3405"]
  R1 = Resistor [tolerance=±5% resistance=220 package=THT]
  LED1 = LED - 5mm [color="Red (633nm)" package="5 mm [THT]"]
  R2 = PHOTOCELL [package=photocell]
  R3 = Resistor [tolerance=±5% resistance=10k package=THT]

nets:
  N1: Part1.IO21, R1.Pin_0
  N2: Part1.GND, LED1.cathode, R3.Pin_0
  N3: Part1.3.3V, R2.P$2
  N4: Part1.IO14_A6, R2.P$1, R3.Pin_1
  N5: R1.Pin_1, LED1.anode
