# Fritzing sketch Huzzah32_Tone_Piezo_WithPOT (saved by Fritzing 0.9.4)
breadboards: 1

parts:
  Part1 = Adafruit HUZZAH32 ESP32 Feather [part_number="Adafruit #3405"]
  Piezo = Piezo Speaker
  Pot1 = POT [package=alps_pot]

nets:
  N1: Part1.A1_DAC1, Pot1.S
  N2: Part1.A0_DAC2, Piezo.pin2
  N3: Part1.GND, Piezo.pin1, Pot1.E
  N4: Part1.3.3V, Pot1.A

notes:
  GPIO #26
