# Fritzing sketch LEDOn_5VOutputPin (saved by Fritzing 0.9.4)

parts:
  Part1 = Arduino Uno (Rev3) [part_number=Uno]
  R1 = Resistor [tolerance=±5% resistance=220 package=THT]
  LED1 = LED - 5mm [color="Red (633nm)" package="5 mm [THT]"]

nets:
  N1: Part1.GND, LED1.cathode
  N2: Part1.5V, R1.Pin_0
  N3: R1.Pin_1, LED1.anode
