# Fritzing sketch LEDWith9VBatteryAnd2.2KOhmResistor-AndButton (saved by Fritzing 0.9.5d)

parts:
  VCC1 = Battery block 9V
  R1 = Resistor [tolerance=±5% resistance=2.2k package=THT]
  LED1 = LED - 5mm [color="Red (633nm)" package="5 mm [THT]"]
  Switch1 = Pushbutton [package="[THT]"]

nets:
  N1: VCC1.-, LED1.cathode
  N2: R1.Pin_0, LED1.anode
  N3: R1.Pin_1, Switch1.Pin_1, Switch1.Pin_2
