# Fritzing sketch LEDWith9VBatteryAnd350OhmResistor (saved by Fritzing 0.9.4)

parts:
  VCC1 = Battery block 9V
  R1 = Resistor [tolerance=±5% resistance=330 package=THT]
  LED1 = LED - 5mm [color="Red (633nm)" package="5 mm [THT]"]
  R2 = Resistor [tolerance=±5% resistance=10 package=THT]
  R3 = Resistor [tolerance=±5% resistance=10 package=THT]

nets:
  N1: VCC1.-, LED1.cathode
  N2: VCC1.+, R1.Pin_1
  N3: R1.Pin_0, R2.Pin_1
  N4: LED1.anode, R3.Pin_0
  N5: R2.Pin_0, R3.Pin_1
