# Fritzing sketch OLED_ArduinoLeonardo_WithBreadboardAndTwoButtons (saved by Fritzing 0.9.4)
breadboards: 1

parts:
  Part1 = Arduino Leonardo (Rev3b)
  Part2 = OLED Monochrome 128x64 1.3 inch [part_number=938]
  S1 = Pushbutton [package="[THT]"]
  S2 = Pushbutton [package="[THT]"]

nets:
  N1: Part1.D2/SDA, Part2.MOSI_SDA
  N2: Part1.D3_PWM/SCL, Part2.SCLK_SCK
  N3: Part1.D4/A6, S1.Pin_3, S1.Pin_4
  N4: Part1.D5_PWM, S2.Pin_3, S2.Pin_4
  5V: Part1.5V, Part2.VIN
  GND: Part1.GND, Part2.GND, S1.Pin_1, S1.Pin_2, S2.Pin_1, S2.Pin_2

custom parts:
  OLED Monochrome 128x64 1.3 inch: These displays are small, only about 1.3" diagonal, but very readable due to the high contrast of an OLED display. This display is made of 128x64 individual white OLED pixels, each one is turned on or off by the controller chip. Because the display makes its own light, no backlight is required. This reduces the power required to run the OLED and is why the display has such high contrast; we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
