# Fritzing sketch OLED_ESP32_WithBreadboard (saved by Fritzing 0.9.4)
breadboards: 1

parts:
  Part3 = Adafruit HUZZAH32 ESP32 Feather [part_number="Adafruit #3405"]
  Part5 = Adafruit LIS3DH Triple-Axis Accelerometer [part_number="Adafruit #2809"]
  FSR = Basic Force Sensing Resistor (FSR) [package=THT]
  S1 = Pushbutton [package="[THT]"]
  S2 = Pushbutton [package="[THT]"]
  S3 = Pushbutton [package="[THT]"]
  R1 = Resistor [tolerance=±5% resistance=10k package=THT]
  Part6 = OLED Monochrome 128x64 1.3 inch [part_number=938]

nets:
  N1: Part3.A0_DAC2, FSR.pin_0, R1.Pin_1
  GND: Part3.GND, Part5.GND, S1.Pin_1, S1.Pin_2, S2.Pin_1, S2.Pin_2, S3.Pin_1, S3.Pin_2, R1.Pin_0, Part6.GND
  3.3V: Part3.3.3V, Part5.VCC, FSR.pin_1, Part6.VIN
  N2: Part3.IO15_A8, S3.Pin_3, S3.Pin_4
  N3: Part3.IO32_A7, S2.Pin_3, S2.Pin_4
  N4: Part3.IO14_A6, S1.Pin_3, S1.Pin_4
  SCL: Part3.SCL, Part5.SCL, Part6.SCLK_SCK
  SDA: Part3.SDA, Part5.SDA, Part6.MOSI_SDA

custom parts:
  Adafruit LIS3DH Triple-Axis Accelerometer: The LIS3DH is a very popular low power triple-axis accelerometer. It's low-cost, but has just about every 'extra' you'd want in an accelerometer: Three axis sensing, 10-bit precision ±2g/±4g/±8g/±16g selectable scaling Both I2C (2 possible addresses) and SPI interface options Interrupt output Multiple data rate options 1 Hz to 5Khz As low as 2uA current draw (just the chip itself, not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
  OLED Monochrome 128x64 1.3 inch: These displays are small, only about 1.3" diagonal, but very readable due to the high contrast of an OLED display. This display is made of 128x64 individual white OLED pixels, each one is turned on or off by the controller chip. Because the display makes its own light, no backlight is required. This reduces the power required to run the OLED and is why the display has such high contrast; we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
