# Fritzing sketch OhmsLaw-ResistorsInSeries-3Resistors2 (saved by Fritzing 0.9.4)

parts:
  VCC1 = Battery block 9V
  R1 = Resistor [tolerance=±5% resistance=470 package=THT]
  R2 = Resistor [tolerance=±5% resistance=680 package=THT]
  R3 = Resistor [tolerance=±5% resistance=150 package=THT]

nets:
  N1: VCC1.-, R3.Pin_1
  N2: VCC1.+, R1.Pin_1
  N3: R1.Pin_0, R2.Pin_1
  N4: R2.Pin_0, R3.Pin_0
