# Fritzing sketch OhmsLawBasic-SolveForCurrent100Ohm (saved by Fritzing 0.9.4)

parts:
  VCC1 = Battery block 9V
  R1 = Resistor [tolerance=±5% resistance=100 package=THT]

nets:
  N1: VCC1.-, R1.Pin_0
  N2: VCC1.+, R1.Pin_1
