# Fritzing sketch PaintIO_ArduinoLeonardo_WithPotentiometers (saved by Fritzing 0.9.4)
breadboards: 1

parts:
  Part1 = Arduino Leonardo (Rev3b)
  Part2 = OLED Monochrome 128x64 1.3 inch [part_number=938]
  Pot1 = POT [package=alps_pot]
  Pot2 = POT [package=alps_pot]
  Pot3 = POT [package=alps_pot]
  S1 = Pushbutton [package="[THT]"]
  S2 = Pushbutton [package="[THT]"]
  S3 = Pushbutton [package="[THT]"]

nets:
  N1: Part1.D2/SDA, Part2.MOSI_SDA
  N2: Part1.D3_PWM/SCL, Part2.SCLK_SCK
  N3: Part1.D4/A6, S1.Pin_3, S1.Pin_4
  N4: Part1.D5_PWM, S2.Pin_3, S2.Pin_4
  N5: Part1.D6_PWM/A7, S3.Pin_3, S3.Pin_4
  5V: Part1.5V, Part2.VIN, Pot1.E, Pot2.E, Pot3.E
  GND: Part1.GND, Part2.GND, Pot1.A, Pot2.A, Pot3.A, S1.Pin_1, S1.Pin_2, S2.Pin_1, S2.Pin_2, S3.Pin_1, S3.Pin_2
  N6: Part1.A0, Pot1.S
  N7: Part1.A1, Pot2.S
  N8: Part1.A2, Pot3.S

custom parts:
  OLED Monochrome 128x64 1.3 inch: These displays are small, only about 1.3" diagonal, but very readable due to the high contrast of an OLED display. This display is made of 128x64 individual white OLED pixels, each one is turned on or off by the controller chip. Because the display makes its own light, no backlight is required. This reduces the power required to run the OLED and is why the display has such high contrast; we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
