# Fritzing sketch Parallax2AxisJoystick_ArduinoLeonardo (saved by Fritzing 0.9.4)
breadboards: 1

parts:
  Part1 = Parallax 2-Axis Joystick
  Part2 = Arduino Leonardo (Rev3b)

nets:
  N1: Part1.L/R_Vcc, Part1.U/D_Vcc, Part2.5V
  N2: Part1.L/R_Out#5, Part2.A0
  N3: Part1.U/D_Out#7, Part2.A1
  N4: Part1.GND#9, Part2.GND

custom parts:
  Parallax 2-Axis Joystick: Description: This is the Parallax 2-Axis Joystick. It contains a spring return thumb joystick mounted to a breakout board. The breakout board breaks out the joysticks connections to .1" pin headers. The joystick's connections are duplicated on both sides of the board for easy use. This part can easily be used on a breadboard due to the .1" pin headers, but can also be soldered into any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
