# Fritzing sketch Photocell_LEDCircuit_Breadboard (saved by Fritzing 0.9.4)
breadboards: 3

parts:
  VCC2 = Battery block 9V
  R1 = Resistor [tolerance=±5% resistance=470 package=THT]
  R5 = PHOTOCELL [package=photocell]
  LED3 = LED - 5mm [color="Red (633nm)" package="5 mm [THT]"]
  R6 = Resistor [tolerance=±5% resistance=220 package=THT]  # not connected
  R4 = Resistor [tolerance=±5% resistance=220 package=THT]
  LED4 = LED - 5mm [color="Red (633nm)" package="5 mm [THT]"]
  R3 = PHOTOCELL [package=photocell]
  Part8 = Arduino Uno (Rev3)
  Part9 = Arduino Uno (Rev3)
  R7 = PHOTOCELL [package=photocell]
  LED5 = LED - 5mm [color="Red (633nm)" package="5 mm [THT]"]
  R9 = Resistor [tolerance=±5% resistance=4.7k package=THT]

nets:
  N1: VCC2.-, LED3.cathode
  N2: VCC2.+, R1.Pin_0
  N3: R1.Pin_1, R3.P$1
  N4: R5.P$1, LED4.anode
  N5: R5.P$2, R4.Pin_0
  N6: LED3.anode, R3.P$2
  N7: R4.Pin_1, Part8.5V
  N8: LED4.cathode, Part8.GND
  N9: Part9.5V, R9.Pin_1
  N10: Part9.GND, R7.P$1, LED5.cathode
  N11: R7.P$2, LED5.anode, R9.Pin_0

notes:
  In series circuits
  Voltage divider
