# Fritzing sketch PotentiometerLEDCircuit9VBattery (saved by Fritzing 0.9.4)

parts:
  VCC2 = Battery block 9V
  R1 = TRIMPOT [package=3386u]
  R2 = Resistor [tolerance=±5% resistance=470 package=THT]
  LED1 = LED - 5mm [color="Red (633nm)" package="5 mm [THT]"]

nets:
  N1: VCC2.-, LED1.cathode
  N2: VCC2.+, R1.CCW
  N3: R1.WIPER, R2.Pin_0
  N4: R2.Pin_1, LED1.anode
