# Fritzing sketch RGBLEDCircuitSchematic (saved by Fritzing 0.9.3b)

parts:
  R1 = Resistor [tolerance=±5% resistance=220 package=THT]
  LED1 = LED - 5mm [color="Red (633nm)" package="5 mm [THT]"]
  V1 = DC Power [voltage=5]
  R2 = Resistor [tolerance=±5% resistance=220 package=THT]
  LED2 = LED - 5mm [color="Red (633nm)" package="5 mm [THT]"]
  R3 = Resistor [tolerance=±5% resistance=220 package=THT]
  LED3 = LED - 5mm [color="Red (633nm)" package="5 mm [THT]"]
  V2 = DC Power [voltage=5]
  LED4 = RGB LED (com. cathode, rgb) [package="5 mm [THT]"]
  R4 = Resistor [tolerance=±5% resistance=220 package=THT]
  R5 = Resistor [tolerance=±5% resistance=220 package=THT]
  R6 = Resistor [tolerance=±5% resistance=220 package=THT]
  LED5 = RGB LED - (4 legs) [package="5 mm [THT]"]
  V3 = DC Power [voltage=5]
  R7 = Resistor [tolerance=±5% resistance=220 package=THT]
  R8 = Resistor [tolerance=±5% resistance=220 package=THT]
  R9 = Resistor [tolerance=±5% resistance=220 package=THT]
  R10 = Resistor [tolerance=±5% resistance=220 package=THT]
  R11 = Resistor [tolerance=±5% resistance=220 package=THT]
  R12 = Resistor [tolerance=±5% resistance=220 package=THT]
  R13 = Resistor [tolerance=±5% resistance=220 package=THT]
  R14 = Resistor [tolerance=±5% resistance=220 package=THT]
  R15 = Resistor [tolerance=±5% resistance=220 package=THT]
  V4 = DC Power [voltage=5]
  LED6 = RGB LED (com. cathode, rgb) [package="5 mm [THT]"]
  LED7 = RGB LED - (4 legs) [package="5 mm [THT]"]
  LED8 = RGB LED (com. cathode, rgb) [package="5 mm [THT]"]  # not connected
  LED9 = RGB LED - (4 legs) [package="5 mm [THT]"]  # not connected

nets:
  N1: R1.Pin_0, LED1.anode
  N2: R1.Pin_1, V1.V-
  GND: LED1.cathode, R2.Pin_1, LED4.common_cathode, LED6.common_cathode
  N3: R2.Pin_0, LED2.cathode
  Pin 3: LED2.anode, R6.Pin_0, R9.Pin_0
  N4: R3.Pin_0, LED3.anode
  N5: R3.Pin_1, V2.V-
  Pin 4: LED3.cathode
  N6: LED4.red_anode, R4.Pin_1
  N7: LED4.green_anode, R5.Pin_1
  N8: LED4.blue_anode, R6.Pin_1
  Pin 6: R4.Pin_0, R8.Pin_0
  Pin 5: R5.Pin_0, R7.Pin_0
  N9: LED5.red_cathode, R8.Pin_1
  N10: LED5.common_anode, V3.V-
  N11: LED5.green_cathode, R7.Pin_1
  N12: LED5.blue_cathode, R9.Pin_1
  Arduino Pin Z: R10.Pin_0, R12.Pin_0
  N13: R10.Pin_1, LED7.blue_cathode
  Arduino Pin X: R11.Pin_0, R14.Pin_0
  N14: R11.Pin_1, LED7.red_cathode
  N15: R12.Pin_1, LED6.blue_anode
  Arduino Pin Y: R13.Pin_0, R15.Pin_0
  N16: R13.Pin_1, LED6.green_anode
  N17: R14.Pin_1, LED6.red_anode
  N18: R15.Pin_1, LED7.green_cathode
  N19: V4.V-, LED7.common_anode

notes:
  Common Cathode
