# Fritzing sketch RgbLED_Diagrams (saved by Fritzing 0.9.3b)
breadboards: 1

parts:
  Part1 = Arduino Uno (Rev3)
  LED1 = RGB LED (com. anode, rbg) [package="5 mm [THT]"]
  R1 = Resistor [tolerance=±5% resistance=220 package="1206 [SMD]"]
  R2 = Resistor [tolerance=±5% resistance=220 package="1206 [SMD]"]
  R3 = Resistor [tolerance=±5% resistance=220 package="1206 [SMD]"]
  Part2 = Arduino Uno (Rev3)
  LED2 = RGB LED (com. anode, rbg) [package="5 mm [THT]"]
  R4 = Resistor [tolerance=±5% resistance=220 package="1206 [SMD]"]
  R5 = Resistor [tolerance=±5% resistance=220 package="1206 [SMD]"]
  R6 = Resistor [tolerance=±5% resistance=220 package="1206 [SMD]"]

nets:
  N1: Part1.D3_PWM, R3.Pin_0
  N2: Part1.D5_PWM, R2.Pin_0
  N3: Part1.D6_PWM, R1.Pin_0
  N4: Part1.5V, LED1.common_anode
  N5: Part2.D3_PWM, R6.Pin_0
  N6: Part2.D5_PWM, R5.Pin_0
  N7: Part2.D6_PWM, R4.Pin_0
  N8: Part2.5V, LED2.common_anode
  N9: LED2.red_cathode, R4.Pin_1
  N10: LED2.blue_cathode, R5.Pin_1
  N11: LED2.green_cathode, R6.Pin_1
