# Fritzing sketch RotaryPotentiometerWithBreadboard (saved by Fritzing 0.9.4)
breadboards: 1

parts:
  VCC3 = Battery block 9V
  R1 = Resistor [tolerance=±5% resistance=330 package=THT]
  R2 = TRIMPOT [package=3386u]
  LED1 = LED - 5mm [color="Red (633nm)" package="5 mm [THT]"]

nets:
  N1: VCC3.-, LED1.cathode
  N2: VCC3.+, R2.CCW
  N3: R1.Pin_0, R2.WIPER
  N4: R1.Pin_1, LED1.anode
