# Fritzing sketch SeriesAndParallel2 (saved by Fritzing 0.9.4)

parts:
  VCC1 = Battery block 9V  # not connected
  R1 = Resistor [tolerance=±5% resistance=100 package=THT]
  R2 = Resistor [tolerance=±5% resistance=150 package=THT]
  R3 = Resistor [tolerance=±5% resistance=1k package=THT]  # not connected
  R4 = Resistor [tolerance=±5% resistance=100 package=THT]
  R5 = Resistor [tolerance=±5% resistance=100 package=THT]  # not connected

nets:
  N1: R1.Pin_1, R2.Pin_0, R4.Pin_0
