# Fritzing sketch SimpleMp3PlayerWithPOT (saved by Fritzing 0.9.5d)
breadboards: 1

parts:
  Part1 = Adafruit VS1053 Headphone FeatherWing [part_number="Adafruit #3357"]  # not connected
  Part2 = Adafruit Feather nRF52840 [part_number=4062]
  S1 = Pushbutton [package="[THT]"]
  S2 = Pushbutton [package="[THT]"]
  POT1 = Breadboard Trimpot

nets:
  N1: Part2.3.3V, POT1.PIN3
  N2: Part2.GND, S1.Pin_1, S1.Pin_2, S2.Pin_1, S2.Pin_2, POT1.PIN1
  N3: Part2.A0, POT1.PIN2
  N4: Part2.D12, S2.Pin_3, S2.Pin_4
  N5: Part2.D13, S1.Pin_3, S1.Pin_4

custom parts:
  Adafruit VS1053 Headphone FeatherWing: Bend all audio files to your will with the Adafruit Music Maker FeatherWing! It's a fun-size version of our Music Maker shield for Arduino! This powerful shield features the VS1053, an encoding/decoding (codec) chip that can decode a wide variety of audio formats such as MP3, AAC, Ogg Vorbis, WMA, MIDI, FLAC, WAV (PCM and ADPCM). You can do all sorts of stuff with the audio as well such as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
  Adafruit Feather nRF52840: The Adafruit Feather nRF52840 Express is our take on an 'all-in-one' Arduino-compatible + Bluetooth Low Energy with built in USB plus battery charging, 1 MB of FLASH and 256KB of SRAM. With native USB it's even ready to join the CircuitPython party. For this chip, we've added Arduino IDE support - you can program the nRF52840 chip directly to take full advantage of the Cortex-M4 processor, and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
