# Fritzing sketch SimpleMp3PlayerWithPOTMicAndLED (saved by Fritzing 0.9.5d)
breadboards: 1

parts:
  Part1 = Adafruit VS1053 Headphone FeatherWing [part_number="Adafruit #3357"]  # not connected
  Part2 = Adafruit Feather nRF52840 [part_number=4062]
  S1 = Pushbutton [package="[THT]"]
  S2 = Pushbutton [package="[THT]"]
  POT1 = Breadboard Trimpot
  Part3 = Adafruit MAX9814 Electret Microphone Amplifier [part_number="Adafruit #1713"]
  C2 = Electrolytic Capacitor [capacitance=100µF voltage=16V package="200 mil [THT, electrolytic]"]
  LED1 = LED - 5mm [color="Red (633nm)" package="5 mm [THT]"]
  R1 = Resistor [tolerance=±5% resistance=220 package=THT]

nets:
  3.3V: Part2.3.3V, POT1.PIN3, Part3.VDD, C2.+
  GND: Part2.GND, S1.Pin_1, S1.Pin_2, S2.Pin_1, S2.Pin_2, POT1.PIN1, Part3.GND, C2.-, R1.Pin_1
  N1: Part2.A0, POT1.PIN2
  N2: Part2.A5, Part3.OUTPUT
  N3: Part2.D11, LED1.anode
  N4: Part2.D12, S2.Pin_3, S2.Pin_4
  N5: Part2.D13, S1.Pin_3, S1.Pin_4
  N6: LED1.cathode, R1.Pin_0

custom parts:
  Adafruit VS1053 Headphone FeatherWing: Bend all audio files to your will with the Adafruit Music Maker FeatherWing! It's a fun-size version of our Music Maker shield for Arduino! This powerful shield features the VS1053, an encoding/decoding (codec) chip that can decode a wide variety of audio formats such as MP3, AAC, Ogg Vorbis, WMA, MIDI, FLAC, WAV (PCM and ADPCM). You can do all sorts of stuff with the audio as well such as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
  Adafruit Feather nRF52840: The Adafruit Feather nRF52840 Express is our take on an 'all-in-one' Arduino-compatible + Bluetooth Low Energy with built in USB plus battery charging, 1 MB of FLASH and 256KB of SRAM. With native USB it's even ready to join the CircuitPython party. For this chip, we've added Arduino IDE support - you can program the nRF52840 chip directly to take full advantage of the Cortex-M4 processor, and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
  Adafruit MAX9814 Electret Microphone Amplifier: Add an ear to your project with this well-designed electret microphone amplifier with AGC. This fully assembled and tested board comes with a 20-20KHz electret microphone soldered on. For the amplification, we use the Maxim MAX9814, a specialty chip that is designed for amplifying electret microphones in situations where the loudness of the audio isn't predictable. This fancy microphone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
