# Fritzing sketch SimpleSerialIn_ArduinoLeonardo (saved by Fritzing 0.9.4)
breadboards: 1

parts:
  LED1 = LED - 5mm [color="Red (633nm)" package="5 mm [THT]"]
  R1 = Resistor [tolerance=±5% resistance=330 package=THT]
  Part2 = Arduino Leonardo (Rev3b)

nets:
  GND: LED1.cathode, Part2.GND
  N1: LED1.anode, R1.Pin_1
  N2: R1.Pin_0, Part2.D13_PWM
