# Fritzing sketch VibroMotorTransistorDiodeCapacitor_ArduinoLeonardo (saved by Fritzing 0.9.4)

parts:
  Part2 = Arduino Leonardo (Rev3b)
  MOTOR1 = Vibration Motor
  NPN_Transistor1 = NPN-Transistor [package="TO92 [THT]"]
  R2 = Resistor [tolerance=±5% resistance=1k package=THT]
  D1 = Rectifier Diode [part_number=1N4001 package="300 mil [THT]"]
  C1 = Ceramic Capacitor [capacitance=0.1µF package="100 mil [THT, multilayer]"]

nets:
  N1: Part2.D3_PWM/SCL, Part2.SCL, R2.Pin_0
  N2: Part2.3V3, MOTOR1.POS, D1.cathode, C1.1
  GND: Part2.GND, NPN_Transistor1.E
  N3: MOTOR1.NEG, NPN_Transistor1.C, D1.anode, C1.0
  N4: NPN_Transistor1.B, R2.Pin_1

custom parts:
  Vibration Motor: An eccentric vibration motor!
