# Fritzing sketch VibroMotorTransistor_ArduinoLeonardo2-3.3V-HilariousLookingVibromotor (saved by Fritzing 0.9.4)

parts:
  Part2 = Arduino Leonardo (Rev3b)
  NPN_Transistor = NPN-Transistor [part_number=2n2222 package="TO92 [THT]"]
  R1 = Resistor [tolerance=±5% resistance=1k package=THT]
  ERM_Motor = Vibration Motor- ROB-08449 [package=vibe-motor-10mm]

nets:
  N1: Part2.D3_PWM/SCL, Part2.SCL, R1.Pin_0
  N2: Part2.5V, ERM_Motor.-
  GND: Part2.GND, NPN_Transistor.E
  N3: NPN_Transistor.B, R1.Pin_1
  N4: NPN_Transistor.C, ERM_Motor.+

notes:
  D3/SCL
  D2/SDA
