# Fritzing sketch VibroMotorTransistor_ArduinoLeonardo2-5V-HilariousLookingVibromotor (saved by Fritzing 0.9.4)

parts:
  Part2 = Arduino Leonardo (Rev3b)
  MOTOR1 = Vibration Motor
  NPN_Transistor1 = NPN-Transistor [package="TO92 [THT]"]
  R2 = Resistor [tolerance=±5% resistance=1k package=THT]

nets:
  N1: Part2.D3_PWM/SCL, Part2.SCL, R2.Pin_0
  N2: Part2.5V, MOTOR1.POS
  GND: Part2.GND, NPN_Transistor1.E
  N3: MOTOR1.NEG, NPN_Transistor1.C
  N4: NPN_Transistor1.B, R2.Pin_1

custom parts:
  Vibration Motor: An eccentric vibration motor!
