# Fritzing sketch VibroMotorTransitor_ArduinoLeonardo_1Pot_WithBreadboard (saved by Fritzing 0.9.4)
breadboards: 1

parts:
  Part2 = Arduino Leonardo (Rev3b)
  Pot1 = POT [package=alps_pot]
  Q1 = NPN-Transistor [package="TO92 [THT]"]
  R1 = Resistor [tolerance=±5% resistance=1k package=THT]
  MOTOR1 = Vibration Motor

nets:
  N1: Part2.D3_PWM/SCL, R1.Pin_1
  N2: Part2.5V, Pot1.E, MOTOR1.POS
  N3: Part2.GND, Pot1.A, Q1.E
  N4: Part2.A0, Pot1.S
  N5: Q1.B, R1.Pin_0
  N6: Q1.C, MOTOR1.NEG

custom parts:
  Vibration Motor: An eccentric vibration motor!
