# Fritzing sketch VibroMotorTransitor_ArduinoLeonardo_1Pot_WithBreadboardAndSchematic (saved by Fritzing 0.9.4)
breadboards: 1

parts:
  Part2 = Arduino Leonardo (Rev3b)
  Pot = POT [package=alps_pot]
  NPN_Transistor = NPN-Transistor [package="TO92 [THT]"]
  R1 = Resistor [tolerance=±5% resistance=1k package=THT]
  MOTOR1 = Vibration Motor

nets:
  N1: Part2.D3_PWM/SCL, Part2.SCL, R1.Pin_1
  5V: Part2.5V, Pot.E, MOTOR1.POS
  GND: Part2.GND, Pot.A, NPN_Transistor.E
  N2: Part2.A0, Pot.S
  N3: NPN_Transistor.B, R1.Pin_0
  N4: NPN_Transistor.C, MOTOR1.NEG

custom parts:
  Vibration Motor: An eccentric vibration motor!
