# Fritzing sketch VibroMotorTransitor_ArduinoLeonardo_1Pot_WithBreadboardAndSchematic2 (saved by Fritzing 0.9.4)
breadboards: 1

parts:
  NPN_Transistor = NPN-Transistor [package="TO92 [THT]"]
  R1 = Resistor [tolerance=±5% resistance=1k package=THT]
  Vibromotor = Vibration Motor- ROB-08449 [package=vibe-motor-10mm]
  Part2 = Arduino Uno (Rev3)

nets:
  GND: NPN_Transistor.E, Part2.GND
  N1: NPN_Transistor.B, R1.Pin_0
  N2: NPN_Transistor.C, Vibromotor.+
  N3: R1.Pin_1, Part2.D5_PWM
  5V: Vibromotor.-
