# Fritzing sketch VibroMotorTransitor_ArduinoLeonardo_WithBreadboardAndSchematic_Incorrect (saved by Fritzing 0.9.4)

parts:
  Part2 = Arduino Leonardo (Rev3b)
  MOTOR1 = Vibration Motor

nets:
  N1: Part2.D3_PWM/SCL, MOTOR1.POS
  GND: Part2.GND, MOTOR1.NEG

custom parts:
  Vibration Motor: An eccentric vibration motor!
